// Logisim project T2.circ as structural Verilog: 1 circuit, main circuit main
module main (
  input  Modo,
  input  Clear,
  output out_3,
  output out_4,
  output out_5,
  output out_6
);

  wire clock_1_out, n7408_1_p1;

  Clock clock_1 (.out(clock_1_out));
  // _74161 74161_1: pin names not known; wires that end beside it: Clear, clock_1_out, out_5, out_4, out_3
  // _7408 7408_1: pin names not known; wires that end beside it: n7408_1_p1, Clear, out_6
  // _74157 74157_1: pin names not known; wires that end beside it: Modo, 1'b0, 1'b1, n7408_1_p1, 1'b0
endmodule
